# Fritzing sketch ESP01_LightMeter (saved by Fritzing 0.9.1b)
breadboards: 1

parts:
  U1 = ESP8266 WiFi Module [part_number=ESP8266]
  P1 = S1133 Si Photodiode [part_number=PT333-3C package="8mm Ceramic [THT]"]
  C1 = Electrolytic Capacitor [capacitance=0.47mF package="100 mil [THT, electrolytic]"]
  R1 = Resistor [tolerance=±5% resistance=220 package=THT]
  Part1 = FTDI Basic Programmer

nets:
  N1: U1.RXD, Part1.TXO
  3.3V: U1.VCC, U1.CH_PD, C1.+, Part1.POWER
  GND: U1.GPIO_0, U1.GND, P1.anode, Part1.GND
  N2: U1.GPIO_2, R1.Pin_1
  N3: U1.TXD, Part1.RXI
  N4: P1.cathode, C1.-, R1.Pin_0

custom parts:
  ESP8266 WiFi Module: Generic WiFi Module based on the ESP8266 with onboard PCB antenna and UART communications
